# Fritzing sketch sensor-receiver-design (saved by Fritzing 0.9.10b)

parts:
  Part1 = Arduino Uno (Rev3) - ICSP
  Rx1 = mystery part, 4 pins [chip_label=?]
  HC-SR04_Sensor_1 = HC-SR04 Ultrasonic Distance Sensor
  HC-SR04_Sensor_2 = HC-SR04 Ultrasonic Distance Sensor
  Part2 = Jtron 1 Channel Optoisolated Relay Module [package=relay]
  J1 = Piezo Speaker
  BAT1 = 12 battery [package=battery]

nets:
  N1: Part1.ICSP_MOSI, Part1.D11_PWM/MOSI, Rx1.pin3
  N2: Part1.D13/SCK, Part2.IN1
  GND: Part1.GND, Rx1.pin1, HC-SR04_Sensor_1.GND, HC-SR04_Sensor_2.GND, Part2.GND
  N3: Part1.D2, HC-SR04_Sensor_1.ECHO
  N4: Part1.D3_PWM, HC-SR04_Sensor_1.TRIG
  N5: Part1.D4, HC-SR04_Sensor_2.TRIG
  N6: Part1.D5_PWM, HC-SR04_Sensor_2.ECHO
  VCC: Part1.5V, Rx1.pin4, HC-SR04_Sensor_1.VCC, HC-SR04_Sensor_2.VCC, Part2.VCC
  N7: Part2.NO, J1.pin2
  N8: Part2.MAIN, BAT1.+
  N9: J1.pin1, BAT1.-

notes:
  443MHz receiver
  one sensor pointed at each seat - either can trigger

custom parts:
  12 battery: 12V lead acid type battery, like the Husqvarna YTH2448 12V 35AH battery. This is the mini version 1/4 the size of the actual battery to be closer to typical breadboard parts (around 2in wide rathher than 7in). The pads in pcb are sized to accomidate up to 14ga wire (as these batterys will deliver high currents.)
